# Fritzing sketch Ada (saved by Fritzing 0.9.3b)
circuit board: 10.0147cm x 5.41049cm
breadboards: 1

parts:
  Part1 = Motor Driver 1A Dual TB6612FNG
  Part2 = InvenSense MPU6050
  U1 = ESP32S-HiLetgo [part_number=ESP32S-HiLetgo]
  DC_Mot_Enc1 = DC Motor with two-phase hall-encoder [part_number=VT-E-G25A-06-177E]
  DC_Mot_Enc2 = DC Motor with two-phase hall-encoder [part_number=VT-E-G25A-06-177E]
  JACK1 = 2.1mm Barrel Jack with Terminal Block
  C1 = Ceramic Capacitor [capacitance=100nF package="100 mil [THT, multilayer]"]
  C2 = Electrolytic Capacitor [capacitance=1µF package="100 mil [THT, electrolytic]"]
  C3 = Ceramic Capacitor [capacitance=100nF package="100 mil [THT, multilayer]"]
  C4 = Electrolytic Capacitor [capacitance=1µF package="100 mil [THT, electrolytic]"]

nets:
  GND: Part1.GND, Part2.GND, U1.GND, DC_Mot_Enc1.pin2, DC_Mot_Enc2.pin2, DC_Mot_Enc2.pin3, DC_Mot_Enc2.pin5, JACK1.NEG, C1.0, C2.-, C3.0, C4.-
  N1: Part1.B01, DC_Mot_Enc2.pin1
  N2: Part1.A01, DC_Mot_Enc1.pin1
  VCC: Part1.VCC, Part2.VCC, U1.3.3, DC_Mot_Enc2.pin6, C3.1, C4.+
  N3: Part1.VM, JACK1.POS, C1.1, C2.+
  N4: Part1.PWMA, U1.GPIO13
  N5: Part1.AIN2, U1.GPIO12
  N6: Part1.AIN1, U1.GPIO14
  N7: Part1.STBY, U1.GPIO27
  N8: Part1.BIN1, U1.GPIO26
  N9: Part1.BIN2, U1.GPIO25
  N10: Part1.PWMB, U1.GPIO33
  N11: Part2.SCL, U1.GPIO22
  N12: Part2.SDA, U1.GPIO3
  N13: U1.GPIO2, DC_Mot_Enc2.pin4
  N14: U1.GPIO4, DC_Mot_Enc1.pin3, DC_Mot_Enc1.pin4
  N15: DC_Mot_Enc1.pin5, DC_Mot_Enc1.pin6

custom parts:
  ESP32S-HiLetgo: HiLetgo ESP-WROOM-32 ESP32 ESP-32S Development Board 2.4GHz Dual-Mode WiFi + Bluetooth Dual Cores Microcontroller The ESP32 integrated with Antenna switches, RF Balun, power amplifiers, low-noise amplifiers, filters, and management modules, and the entire solution occupies the least area of PCB. 2.4 GHz Wi-Fi plus Bluetooth dual-mode chip, with TSMC Ultra-low power consumption 40nm technology,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
